// Logisim project subtask_one_19053031.circ as structural Verilog: 1 circuit, main circuit main
module main (
  input  Button_0,
  input  Button_1,
  input  Button_2,
  input  Button_3,
  input  Button_4,
  input  Button_5,
  input  Button_6,
  input  Button_7,
  output out_9,
  output out_10,
  output out_11,
  output out_12
);

  Priority_Encoder priority_encoder_1 (
    .in0(Button_0), .in1(Button_1), .in2(Button_2), .in3(Button_3), .in4(Button_4), .in5(Button_5),
    .in6(Button_6), .in7(Button_7), .out({out_9, out_10, out_12}), .gs(out_11));  // open: en_in, en_out
endmodule
