// Logisim project subtask_two_analyse_19053031.circ as structural Verilog
module main (
  input  E0,
  input  E1,
  input  E2,
  output S1,
  output S2,
  output S3,
  output S4,
  output S5,
  output S6,
  output S7
);

  wire and_1_out, and_2_out, and_3_out, and_4_out, and_5_out, and_6_out, and_7_out, and_8_out, and_9_out,
       and_10_out, and_11_out, and_12_out, and_13_out, and_14_out, and_15_out, and_16_out, not_1_out,
       not_2_out, not_3_out, not_4_out, not_5_out, not_6_out, not_7_out, not_8_out, not_9_out, not_10_out,
       not_11_out, not_12_out, not_13_out, not_14_out, not_15_out, not_16_out, not_17_out, not_18_out,
       not_19_out, not_20_out, not_21_out;

  not not_1 (not_1_out, E0);
  not not_2 (not_2_out, E1);
  not not_3 (not_3_out, E2);
  not not_4 (not_4_out, E1);
  not not_5 (not_5_out, E2);
  not not_6 (not_6_out, E1);
  not not_7 (not_7_out, E2);
  not not_8 (not_8_out, E0);
  not not_9 (not_9_out, E2);
  not not_10 (not_10_out, E1);
  not not_11 (not_11_out, E2);
  not not_12 (not_12_out, E0);
  not not_13 (not_13_out, E2);
  not not_14 (not_14_out, E2);
  not not_15 (not_15_out, E0);
  not not_16 (not_16_out, E2);
  not not_17 (not_17_out, E0);
  not not_18 (not_18_out, E2);
  not not_19 (not_19_out, E1);
  not not_20 (not_20_out, E1);
  and and_1 (and_1_out, not_1_out, E1);
  and and_2 (and_2_out, E0, not_2_out);
  and and_3 (and_3_out, E0, not_3_out);
  and and_4 (and_4_out, not_4_out, not_5_out);
  and and_5 (and_5_out, E0, not_6_out);
  and and_6 (and_6_out, E0, not_7_out);
  and and_7 (and_7_out, not_8_out, not_9_out);
  and and_8 (and_8_out, E0, E2);
  not not_21 (not_21_out, E0);
  and and_9 (and_9_out, not_10_out, not_11_out);
  and and_10 (and_10_out, E1, E2);
  and and_11 (and_11_out, not_12_out, not_13_out);
  and and_12 (and_12_out, E1, not_14_out);
  and and_13 (and_13_out, not_15_out, not_16_out);
  and and_14 (and_14_out, not_17_out, E1);
  and and_15 (and_15_out, E1, not_18_out);
  and and_16 (and_16_out, E0, not_19_out, E2);
  or or_1 (S7, not_20_out, E2, E0);
  or or_2 (S1, and_1_out, and_2_out, and_3_out);
  or or_3 (S2, and_4_out, and_5_out, and_6_out);
  or or_4 (S3, and_7_out, E1, and_8_out);
  or or_5 (S4, not_21_out, and_9_out, and_10_out);
  or or_6 (S5, and_11_out, and_12_out);
  or or_7 (S6, and_13_out, and_14_out, and_15_out, and_16_out);
endmodule
